# Fritzing sketch tank (saved by Fritzing 0.6.5b)
breadboards: 1

parts:
  Arduino1 = Arduino
  IC1 = L293D [package=THT]  # not connected
  IC2 = L293D [package=THT]
  VCC1 = Battery block 9V
  U1 = mystery part, 3 pins [chip_label=IR spacing=300mil]
  M1 = Stepper Motor - Bipolar

nets:
  N1: Arduino1.D9, IC2.In_1
  N2: Arduino1.D8, IC2.In_2
  N3: Arduino1.D7, IC2.In_3
  N4: Arduino1.D6, IC2.In_4
  N5: Arduino1.D3, U1.pin2
  N6: IC2.Enable_1, IC2.Enable_2, IC2.+V, U1.pin3
  N7: IC2.Out_1_(_Controlled_by_Enable_1_), M1.C
  N8: IC2.0V, VCC1.-, U1.pin1
  N9: IC2.Out_2_(_Controlled_by_Enable_1_), M1.A
  N10: IC2.+Vmotor, VCC1.+
  N11: IC2.Out_3_(_Controlled_by_Enable_2_), M1.D
  N12: IC2.Out_4_(_Controlled_by_Enable_2_), M1.B
